// Logisim project 16BitALU.circ as structural Verilog: 1 circuit, main circuit main
module main (
  input  [5:0] in_1,
  input  [15:0] in_2,
  input  [15:0] in_3,
  output [1:0] out_4,
  output [15:0] out_5
);

  wire main_1_out_6, main_2_out_6, main_3_out_6, main_4_out_6, main_5_out_6, main_6_out_6, main_7_out_6,
       main_8_out_6, main_9_out_6, main_10_out_6, main_11_out_6, main_12_out_6, main_13_out_6, main_14_out_6,
       main_15_out_6;
  wire [5:0] main_1_out_7, main_2_out_7, main_3_out_7, main_4_out_7, main_5_out_7, main_6_out_7,
       main_7_out_7, main_8_out_7, main_9_out_7, main_10_out_7, main_11_out_7, main_12_out_7, main_13_out_7,
       main_14_out_7, main_15_out_7;

  _1BitALU_main main_1 (
    .out_5(out_5[0]), .in_3(in_2[0]), .in_4(in_3[0]), .out_6(main_1_out_6), .in_2(1'b0), .in_1(in_1),
    .out_7(main_1_out_7));
  _1BitALU_main main_2 (
    .out_5(out_5[1]), .in_3(in_2[1]), .in_4(in_3[1]), .out_6(main_2_out_6), .in_2(main_1_out_6),
    .in_1(main_1_out_7), .out_7(main_2_out_7));
  _1BitALU_main main_3 (
    .out_5(out_5[2]), .in_3(in_2[2]), .in_4(in_3[2]), .out_6(main_3_out_6), .in_2(main_2_out_6),
    .in_1(main_2_out_7), .out_7(main_3_out_7));
  _1BitALU_main main_4 (
    .out_5(out_5[3]), .in_3(in_2[3]), .in_4(in_3[3]), .out_6(main_4_out_6), .in_2(main_3_out_6),
    .in_1(main_3_out_7), .out_7(main_4_out_7));
  _1BitALU_main main_5 (
    .out_5(out_5[4]), .in_3(in_2[4]), .in_4(in_3[4]), .out_6(main_5_out_6), .in_2(main_4_out_6),
    .in_1(main_4_out_7), .out_7(main_5_out_7));
  _1BitALU_main main_6 (
    .out_5(out_5[5]), .in_3(in_2[5]), .in_4(in_3[5]), .out_6(main_6_out_6), .in_2(main_5_out_6),
    .in_1(main_5_out_7), .out_7(main_6_out_7));
  _1BitALU_main main_7 (
    .out_5(out_5[6]), .in_3(in_2[6]), .in_4(in_3[6]), .out_6(main_7_out_6), .in_2(main_6_out_6),
    .in_1(main_6_out_7), .out_7(main_7_out_7));
  _1BitALU_main main_8 (
    .out_5(out_5[7]), .in_3(in_2[7]), .in_4(in_3[7]), .out_6(main_8_out_6), .in_2(main_7_out_6),
    .in_1(main_7_out_7), .out_7(main_8_out_7));
  _1BitALU_main main_9 (
    .out_5(out_5[8]), .in_3(in_2[8]), .in_4(in_3[8]), .out_6(main_9_out_6), .in_2(main_8_out_6),
    .in_1(main_8_out_7), .out_7(main_9_out_7));
  _1BitALU_main main_10 (
    .out_5(out_5[9]), .in_3(in_2[9]), .in_4(in_3[9]), .out_6(main_10_out_6), .in_2(main_9_out_6),
    .in_1(main_9_out_7), .out_7(main_10_out_7));
  _1BitALU_main main_11 (
    .out_5(out_5[10]), .in_3(in_2[10]), .in_4(in_3[10]), .out_6(main_11_out_6), .in_2(main_10_out_6),
    .in_1(main_10_out_7), .out_7(main_11_out_7));
  _1BitALU_main main_12 (
    .out_5(out_5[11]), .in_3(in_2[11]), .in_4(in_3[11]), .out_6(main_12_out_6), .in_2(main_11_out_6),
    .in_1(main_11_out_7), .out_7(main_12_out_7));
  _1BitALU_main main_13 (
    .out_5(out_5[12]), .in_3(in_2[12]), .in_4(in_3[12]), .out_6(main_13_out_6), .in_2(main_12_out_6),
    .in_1(main_12_out_7), .out_7(main_13_out_7));
  _1BitALU_main main_14 (
    .out_5(out_5[13]), .in_3(in_2[13]), .in_4(in_3[13]), .out_6(main_14_out_6), .in_2(main_13_out_6),
    .in_1(main_13_out_7), .out_7(main_14_out_7));
  _1BitALU_main main_15 (
    .out_5(out_5[14]), .in_3(in_2[14]), .in_4(in_3[14]), .out_6(main_15_out_6), .in_2(main_14_out_6),
    .in_1(main_14_out_7), .out_7(main_15_out_7));
  _1BitALU_main main_16 (
    .out_5(out_4[1]), .in_3(in_2[15]), .in_4(in_3[15]), .in_2(main_15_out_6), .in_1(main_15_out_7));  // open: out_6, out_7
  nor nor_1 (out_4[0], out_5[0], out_5[1], out_5[2], out_5[3], out_5[4], out_5[5], out_5[6], out_5[7], out_5[8], out_5[9], out_5[10], out_5[11], out_5[12], out_5[13], out_5[14], out_4[1]);

  assign out_5[15] = out_4[1];
endmodule
