// Logisim project 1BitALU.circ as structural Verilog: 1 circuit, main circuit main
module main (
  input  [5:0] in_1,
  input  in_2,
  input  in_3,
  input  in_4,
  output out_5,
  output out_6,
  output [5:0] out_7
);

  wire and_1_out, and_2_out, and_3_out, and_4_out, and_5_out, main_1_out_4, not_1_out, not_2_out, not_3_out,
       or_1_out, xor_1_out, xor_2_out;

  not not_1 (not_1_out, in_1[5]);
  not not_2 (not_2_out, in_1[3]);
  and and_1 (and_1_out, not_1_out, in_3);
  and and_2 (and_2_out, not_2_out, in_4);
  FullAdder_main main_1 (.out_4(main_1_out_4), .out_5(out_6), .in_2(xor_1_out), .in_3(xor_2_out), .in_1(in_2));
  xor xor_1 (xor_1_out, and_1_out, in_1[4]);
  xor xor_2 (xor_2_out, and_2_out, in_1[2]);
  not not_3 (not_3_out, in_1[1]);
  and and_3 (and_3_out, xor_1_out, xor_2_out);
  and and_4 (and_4_out, main_1_out_4, in_1[1]);
  or or_1 (or_1_out, and_4_out, and_5_out);
  and and_5 (and_5_out, not_3_out, and_3_out);
  xor xor_3 (out_5, in_1[0], or_1_out);

  assign out_7 = in_1;
endmodule
