// Logisim project CentralProcessingUnit.circ as structural Verilog: 1 circuit, main circuit main
module main (
  input  [15:0] Instruction,
  input  Clock,
  input  [15:0] inMemory,
  input  Reset,
  output [15:0] outMemory,
  output writeMemory,
  output [15:0] addressMemory,
  output Clear_Screen,
  output Refresh_Screen,
  output [15:0] program_counter_out
);

  wire main_1_a_reg_inm, main_1_alu_instr, main_1_jump, main_1_pc_plus_plus, main_1_write_register_a,
       main_1_write_register_d;
  wire [1:0] main_2_out_4;
  wire [5:0] main_1_alu_control;
  wire [15:0] D_Register_q, multiplexer_1_out, multiplexer_2_out;

  Multiplexer #(.width(16), .disabled(0), .enable("false")) multiplexer_1 (
    .in0(outMemory), .in1(Instruction), .out(multiplexer_1_out), .sel(main_1_alu_instr));
  ControlUnit_main main_1 (
    .instruction(Instruction), .alu_flags(main_2_out_4), .alu_instr(main_1_alu_instr),
    .write_Register_A(main_1_write_register_a), .write_Register_D(main_1_write_register_d),
    .write_Memory__A(writeMemory), .a_reg_inM(main_1_a_reg_inm), .alu_control(main_1_alu_control),
    .pc_plus_plus(main_1_pc_plus_plus), .jump(main_1_jump), .clock(Clock), .Refresh(Refresh_Screen),
    .Clear(Clear_Screen));
  Register #(.width(16)) A_Register (
    .D(multiplexer_1_out), .Q(addressMemory), .clk(main_1_write_register_a));  // open: en, clr
  Multiplexer #(.width(16), .disabled(0), .enable("false")) multiplexer_2 (
    .in0(addressMemory), .in1(inMemory), .out(multiplexer_2_out), .sel(main_1_a_reg_inm));
  Register #(.width(16)) D_Register (.D(outMemory), .Q(D_Register_q), .clk(main_1_write_register_d));  // open: en, clr
  _16BitALU_main main_2 (
    .in_3(multiplexer_2_out), .in_2(D_Register_q), .out_5(outMemory), .in_1(main_1_alu_control),
    .out_4(main_2_out_4));
  ProgramCounter_main main_3 (
    .in_1(addressMemory), .in_2(Reset), .in_3(main_1_jump), .in_4(main_1_pc_plus_plus),
    .out_5(program_counter_out));
endmodule
