// Logisim project Computer.circ as structural Verilog: 1 circuit, main circuit main
module main (
);

  wire button_1_out, clock_1_out, main_2_refresh_screen, main_2_writememory, main_3_out_6;
  wire [5:0] main_3_out_7;
  wire [15:0] main_1_out_2, main_2_addressmemory, main_2_outmemory, main_2_program_counter_out, main_3_out_4,
       main_3_out_5;
  wire [31:0] main_4_out_6, main_4_out_7, main_4_out_8, main_4_out_9, main_4_out_10, main_4_out_11,
       main_4_out_12, main_4_out_13, main_4_out_14, main_4_out_15, main_4_out_16, main_4_out_17,
       main_4_out_18, main_4_out_19, main_4_out_20, main_4_out_21, main_4_out_22, main_4_out_23,
       main_4_out_24, main_4_out_25, main_4_out_26, main_4_out_27, main_4_out_28, main_4_out_29,
       main_4_out_30, main_4_out_31, main_4_out_32, main_4_out_33, main_4_out_34, main_4_out_35,
       main_4_out_36, main_4_out_37;

  Clock clock_1 (.out(clock_1_out));
  ReadOnlyMemory_main main_1 (.in_1(main_2_program_counter_out), .out_2(main_1_out_2));
  Button button_1 (.out(button_1_out));
  CentralProcessingUnit_main main_2 (
    .Instruction(main_1_out_2), .inMemory(main_3_out_4), .Reset(button_1_out), .outMemory(main_2_outmemory),
    .writeMemory(main_2_writememory), .addressMemory(main_2_addressmemory),
    .program_counter_out(main_2_program_counter_out), .Clock(clock_1_out),
    .Refresh_Screen(main_2_refresh_screen));
  RandomAccessMemory_main main_3 (
    .in_1(main_2_addressmemory), .in_2(main_2_outmemory), .in_3(main_2_writememory), .out_4(main_3_out_4),
    .out_6(main_3_out_6), .out_7(main_3_out_7), .out_5(main_3_out_5));
  Screen_main main_4 (
    .Refresh(main_2_refresh_screen), .Reset(button_1_out), .Data(main_3_out_5), .Address(main_3_out_7),
    .Write(main_3_out_6), .out_6(main_4_out_6), .out_7(main_4_out_7), .out_8(main_4_out_8),
    .out_9(main_4_out_9), .out_10(main_4_out_10), .out_11(main_4_out_11), .out_12(main_4_out_12),
    .out_13(main_4_out_13), .out_14(main_4_out_14), .out_15(main_4_out_15), .out_16(main_4_out_16),
    .out_17(main_4_out_17), .out_18(main_4_out_18), .out_19(main_4_out_19), .out_20(main_4_out_20),
    .out_21(main_4_out_21), .out_22(main_4_out_22), .out_23(main_4_out_23), .out_24(main_4_out_24),
    .out_25(main_4_out_25), .out_26(main_4_out_26), .out_27(main_4_out_27), .out_28(main_4_out_28),
    .out_29(main_4_out_29), .out_30(main_4_out_30), .out_31(main_4_out_31), .out_32(main_4_out_32),
    .out_33(main_4_out_33), .out_34(main_4_out_34), .out_35(main_4_out_35), .out_36(main_4_out_36),
    .out_37(main_4_out_37));
  DotMatrix #(.inputtype("row"), .matrixcols(32), .matrixrows(32)) dotmatrix_1 (
    .row0(main_4_out_6), .row1(main_4_out_7), .row2(main_4_out_8), .row3(main_4_out_9), .row4(main_4_out_10),
    .row5(main_4_out_11), .row6(main_4_out_12), .row7(main_4_out_13), .row8(main_4_out_14),
    .row9(main_4_out_15), .row10(main_4_out_16), .row11(main_4_out_17), .row12(main_4_out_18),
    .row13(main_4_out_19), .row14(main_4_out_20), .row15(main_4_out_21), .row16(main_4_out_22),
    .row17(main_4_out_23), .row18(main_4_out_24), .row19(main_4_out_25), .row20(main_4_out_26),
    .row21(main_4_out_27), .row22(main_4_out_28), .row23(main_4_out_29), .row24(main_4_out_30),
    .row25(main_4_out_31), .row26(main_4_out_32), .row27(main_4_out_33), .row28(main_4_out_34),
    .row29(main_4_out_35), .row30(main_4_out_36), .row31(main_4_out_37));
endmodule
