// Logisim project ControlUnit.circ as structural Verilog: 1 circuit, main circuit main
module main (
  input  [15:0] instruction,
  input  clock,
  input  [1:0] alu_flags,
  output alu_instr,
  output write_Register_A,
  output write_Register_D,
  output write_Memory__A,
  output a_reg_inM,
  output Refresh,
  output [5:0] alu_control,
  output Clear,
  output pc_plus_plus,
  output jump
);

  wire and_1_out, and_2_out, and_3_out, and_4_out, and_5_out, and_6_out, and_7_out, and_8_out,
       decoder_1_out1, decoder_1_out2, decoder_1_out3, decoder_1_out4, decoder_1_out5, decoder_1_out6,
       decoder_1_out7, not_2_out, or_1_out, or_3_out;
  wire [15:0] multiplexer_1_out;

  not not_1 (alu_instr, instruction[15]);
  Multiplexer #(.width(16), .disabled(0), .enable("false")) multiplexer_1 (
    .in0({16{1'b0}}), .in1(instruction),
    .out({multiplexer_1_out[15], Refresh, Clear, a_reg_inM, alu_control, multiplexer_1_out[5:0]}),
    .sel(instruction[15]));
  Decoder #(.select(3), .disabled(0), .enable("false")) decoder_1 (
    .out1(decoder_1_out1), .out2(decoder_1_out2), .out3(decoder_1_out3), .out4(decoder_1_out4),
    .out5(decoder_1_out5), .out6(decoder_1_out6), .out7(decoder_1_out7), .sel(multiplexer_1_out[2:0]));  // open: out0
  and and_1 (and_1_out, alu_instr, clock);
  and and_2 (and_2_out, clock, multiplexer_1_out[5]);
  and and_3 (and_3_out, ~alu_flags[0], ~alu_flags[1], decoder_1_out1);  // AND_Gate
  and and_4 (and_4_out, alu_flags[0], ~alu_flags[1], decoder_1_out2);  // AND_Gate
  and and_5 (and_5_out, ~alu_flags[1], decoder_1_out3);  // AND_Gate
  and and_6 (and_6_out, ~alu_flags[0], alu_flags[1], decoder_1_out4);  // AND_Gate
  and and_7 (and_7_out, ~alu_flags[0], decoder_1_out5);  // AND_Gate
  or or_1 (or_1_out, alu_flags[0], alu_flags[1]);
  and and_8 (and_8_out, or_1_out, decoder_1_out6);
  or or_2 (write_Register_A, and_1_out, and_2_out);
  not not_2 (not_2_out, or_3_out);
  or or_3 (or_3_out, and_3_out, and_4_out, and_5_out, and_6_out, and_7_out, and_8_out, decoder_1_out7);
  and and_9 (write_Register_D, clock, multiplexer_1_out[4]);
  and and_10 (write_Memory__A, clock, multiplexer_1_out[3]);
  and and_11 (pc_plus_plus, not_2_out, clock);
  and and_12 (jump, or_3_out, clock);
endmodule
