// Logisim project ProgramCounter.circ as structural Verilog: 1 circuit, main circuit main
module main (
  input  [15:0] in_1,
  input  in_2,
  input  in_3,
  input  in_4,
  output [15:0] out_5
);

  wire buffer_1_out, buffer_2_out, buffer_3_out, buffer_4_out, or_1_out;

  buf buffer_1 (buffer_1_out, in_3);
  buf buffer_2 (buffer_2_out, buffer_1_out);
  buf buffer_3 (buffer_3_out, buffer_4_out);
  buf buffer_4 (buffer_4_out, in_4);
  or or_1 (or_1_out, in_3, in_4);
  Counter #(.width(16), .max('hffff), .trigger("falling")) counter_1 (
    .load(buffer_2_out), .D(in_1), .count(buffer_3_out), .Q(out_5), .clk(or_1_out), .clr(in_2));  // open: carry
endmodule
