// Logisim project RandomAccessMemory.circ as structural Verilog: 1 circuit, main circuit main
module main (
  input  [15:0] in_1,
  input  [15:0] in_2,
  input  in_3,
  output [15:0] out_4,
  output [15:0] out_5,
  output out_6,
  output [3:0] out_7
);

  wire and_1_out;

  and and_1 (and_1_out, in_1[4], in_1[5], in_1[6], in_1[7], in_1[8], in_1[9], in_1[11], in_1[12], in_1[13], in_1[14], in_1[15], in_1[10]);
  RAM #(.addrWidth(16), .dataWidth(16), .bus("separate")) ram_1 (
    .addr(in_1), .din(in_2), .data(out_4), .str(in_3), .clk(in_3));  // open: sel, ld, clr
  and and_2 (out_6, in_3, and_1_out);

  assign out_5 = in_2;
  assign out_7 = in_1[3:0];
endmodule
