// Logisim project ReadOnlyMemory.circ as structural Verilog: 1 circuit, main circuit main
module main (
  input  [15:0] in_1,
  output [15:0] out_2
);

  ROM #(.addrWidth(16), .dataWidth(16)) rom_1 (.addr(in_1), .data(out_2));  // open: sel
endmodule
